// Logisim project Taller1.circ as structural Verilog: 10 circuits, main circuit verificador
module sumador_simple (
  input  A,
  input  B,
  output S,
  output Cout
);

  xor xor_1 (S, A, B);
  and and_1 (Cout, A, B);
endmodule

module sumador_completo (
  input  Cin,
  input  A,
  input  B,
  output S,
  output Cout
);

  wire sumador_simple_1_cout, sumador_simple_1_s, sumador_simple_2_cout;

  sumador_simple sumador_simple_1 (.A(A), .B(B), .S(sumador_simple_1_s), .Cout(sumador_simple_1_cout));
  sumador_simple sumador_simple_2 (.A(Cin), .B(sumador_simple_1_s), .S(S), .Cout(sumador_simple_2_cout));
  or or_1 (Cout, sumador_simple_2_cout, sumador_simple_1_cout);
endmodule

module sumador_4 (
  input  Cin,
  input  [3:0] A,
  input  [3:0] B,
  output [3:0] S,
  output Cout
);

  wire sumador_completo_1_cout, sumador_completo_2_cout, sumador_completo_3_cout;

  sumador_completo sumador_completo_1 (.Cin(Cin), .A(A[0]), .B(B[0]), .S(S[0]), .Cout(sumador_completo_1_cout));
  sumador_completo sumador_completo_2 (
    .Cin(sumador_completo_1_cout), .A(A[1]), .B(B[1]), .S(S[1]), .Cout(sumador_completo_2_cout));
  sumador_completo sumador_completo_3 (
    .Cin(sumador_completo_2_cout), .A(A[2]), .B(B[2]), .S(S[2]), .Cout(sumador_completo_3_cout));
  sumador_completo sumador_completo_4 (.Cin(sumador_completo_3_cout), .A(A[3]), .B(B[3]), .S(S[3]), .Cout(Cout));
  Hex_Digit_Display hex_digit_display_1 (.value(S));  // open: dp
endmodule

module comparador_cero (
  input  [3:0] A,
  output Z
);

  wire or_1_out, or_2_out, or_3_out;

  or or_1 (or_1_out, A[0], A[1]);
  or or_2 (or_2_out, or_1_out, A[2]);
  or or_3 (or_3_out, or_2_out, A[3]);
  not not_1 (Z, or_3_out);

  // Notes on the sheet:
  //   Otra forma es con 3 AND y 3 NOT, pues not(A+B+C)=not(A).not(B).not(C) 
endmodule

module sumador_flags (
  input  Cin,
  input  [3:0] A,
  input  [3:0] B,
  output [3:0] S,
  output N,
  output Z,
  output V,
  output C
);

  wire and_1_out, and_2_out, and_3_out, and_4_out, not_1_out, not_2_out, not_3_out;

  sumador_4 sumador_4_1 (.Cin(Cin), .A(A), .B(B), .S({N, S[2:0]}), .Cout(C));
  not not_1 (not_1_out, A[3]);
  not not_2 (not_2_out, B[3]);
  and and_1 (and_1_out, not_1_out, not_2_out);
  and and_2 (and_2_out, A[3], B[3]);
  not not_3 (not_3_out, N);
  and and_3 (and_3_out, N, and_1_out);
  and and_4 (and_4_out, not_3_out, and_2_out);
  comparador_cero comparador_cero_1 (.A({N, S[2:0]}), .Z(Z));
  or or_1 (V, and_3_out, and_4_out);
  Hex_Digit_Display hex_digit_display_1 (.value({N, S[2:0]}));  // open: dp

  assign S[3] = N;
endmodule

module incrementador_4 (
  input  [3:0] A,
  output [3:0] S
);

  Hex_Digit_Display hex_digit_display_1 (.value(S));  // open: dp
  sumador_flags sumador_flags_1 (.Cin(1'b0), .A(A), .B(4'b0001), .S(S));  // open: N, Z, V, C

  // Notes on the sheet:
  //   Incrementador de 4 bits. El mismo tendr´a una entrada A de cuatro bits y una salida: S. 
  //   La salida deber´a expresar el resultado de incrementar la entrada en una unidad.
endmodule

module inversor_4 (
  input  [3:0] A,
  input  INV,
  output [3:0] S
);

  wire [3:0] incrementador_4_1_s, xor_1_out;

  xor xor_1 (xor_1_out[0], A[0], INV);
  xor xor_2 (xor_1_out[1], A[1], INV);
  xor xor_3 (xor_1_out[2], A[2], INV);
  xor xor_4 (xor_1_out[3], A[3], INV);
  incrementador_4 incrementador_4_1 (.A(xor_1_out), .S(incrementador_4_1_s));
  Hex_Digit_Display hex_digit_display_1 (.value(S));  // open: dp
  Multiplexer #(.width(4)) multiplexer_1 (.in0(xor_1_out), .in1(incrementador_4_1_s), .out(S), .sel(INV));

  // Notes on the sheet:
  //   No existe inverso aditivo para el 1000. 
  //   En este caso al calcularlo me devuelve el mismo numero
endmodule

module ALU (
  input  [3:0] A,
  input  [3:0] B,
  input  [1:0] OP,
  output N,
  output Z,
  output V,
  output C,
  output [3:0] S
);

  wire and_5_out, and_6_out, comp_8_1_z, comparador_cero_1_z, comparador_cero_2_z, not_1_out,
       sumador_flags_1_c, sumador_flags_1_n, sumador_flags_1_v, sumador_flags_1_z, xor_1_out, xor_2_out,
       xor_3_out;
  wire [3:0] and_1_out, inversor_4_1_s, or_1_out, sumador_flags_1_s;

  and and_1 (and_1_out[0], A[0], B[0]);
  and and_2 (and_1_out[1], A[1], B[1]);
  and and_3 (and_1_out[2], A[2], B[2]);
  and and_4 (and_1_out[3], A[3], B[3]);
  or or_1 (or_1_out[0], A[0], B[0]);
  or or_2 (or_1_out[1], A[1], B[1]);
  or or_3 (or_1_out[2], A[2], B[2]);
  or or_4 (or_1_out[3], A[3], B[3]);
  sumador_flags sumador_flags_1 (
    .Cin(1'b0), .A(A), .B(inversor_4_1_s), .S(sumador_flags_1_s), .N(sumador_flags_1_n),
    .Z(sumador_flags_1_z), .V(sumador_flags_1_v), .C(sumador_flags_1_c));
  comparador_cero comparador_cero_1 (.A(B), .Z(comparador_cero_1_z));
  inversor_4 inversor_4_1 (.A(B), .INV(OP[0]), .S(inversor_4_1_s));
  comp_8 comp_8_1 (.A(B), .Z(comp_8_1_z));
  xor xor_1 (xor_1_out, sumador_flags_1_c, OP[0]);
  and and_5 (and_5_out, comparador_cero_1_z, OP[0]);
  Multiplexer #(.select(2)) multiplexer_1 (
    .in0(sumador_flags_1_n), .in1(sumador_flags_1_n), .in2(S[3]), .in3(S[3]), .out(N), .sel(OP));
  Multiplexer #(.select(2), .width(4)) multiplexer_2 (
    .in0(sumador_flags_1_s), .in1(sumador_flags_1_s), .in2(and_1_out), .in3(or_1_out), .out(S), .sel(OP));
  xor xor_2 (xor_2_out, xor_1_out, and_5_out);
  and and_6 (and_6_out, comp_8_1_z, OP[0]);
  xor xor_3 (xor_3_out, sumador_flags_1_v, and_6_out);
  Multiplexer #(.select(2)) multiplexer_3 (
    .in0(sumador_flags_1_z), .in1(sumador_flags_1_z), .in2(comparador_cero_2_z), .in3(comparador_cero_2_z),
    .out(Z), .sel(OP));
  not not_1 (not_1_out, OP[1]);
  Hex_Digit_Display hex_digit_display_1 (.value(S));  // open: dp
  comparador_cero comparador_cero_2 (.A(S), .Z(comparador_cero_2_z));
  and and_7 (C, not_1_out, xor_2_out);
  and and_8 (V, not_1_out, xor_3_out);
endmodule

module verificador (
  output [3:0] out_1,
  output [3:0] out_2,
  output [1:0] out_3,
  output halt,
  output N,
  output Z,
  output V,
  output C,
  output [3:0] res
);

  wire clock_1_out;

  Clock clock_1 (.out(clock_1_out));
  Counter #(.max('h3ff), .width(10)) counter_1 (
    .clk(clock_1_out), .carry(halt), .Q({out_3, out_2, out_1}));  // open: clr, load, up, count, D
  ALU alu_1 (.A(out_1), .B(out_2), .OP(out_3), .N(N), .Z(Z), .V(V), .C(C), .S(res));
endmodule

module comp_8 (
  input  [3:0] A,
  output Z
);

  wire not_1_out, or_1_out, or_2_out, or_3_out;

  or or_1 (or_1_out, A[0], A[1]);
  or or_2 (or_2_out, or_1_out, A[2]);
  not not_1 (not_1_out, A[3]);
  or or_3 (or_3_out, or_2_out, not_1_out);
  not not_2 (Z, or_3_out);
endmodule
